# Fritzing sketch scheme (saved by Fritzing 0.9.3b)

parts:
  Sensor = Soil Moisture Sensor
  Microcontroller = Arduino Nano (Rev3.0)
  IRF520 = MOSFET-NCHANNEL [package=to220v]
  R1 = Resistor [tolerance=±5% resistance=1k package="2512 [SMD]"]
  Pump = DC Motor

nets:
  N1: Sensor.VCC, Microcontroller.D2
  N2: Sensor.SIG, Microcontroller.A0
  GND: Sensor.GND, Microcontroller.GND, IRF520.S, R1.Pin_0
  N3: Microcontroller.D3, IRF520.G, R1.Pin_1
  N4: Microcontroller.5V, Pump.pin_2
  N5: IRF520.D, Pump.pin_1
